// Logisim project JoseMikaeldaSilvaAlves-ThiagoHenriqueFonsecaPereira.circ as structural Verilog: 4 circuits, main circuit Main
module cache_line (
  input  [27:0] In_tag,
  input  [31:0] In_data,
  input  We,
  input  [1:0] In_Offset,
  input  Clock,
  input  Reset,
  output [27:0] Out_tag,
  output [31:0] Out_data,
  output Out_valid
);
endmodule

module cache (
  input  [31:0] Input_data,
  input  [31:0] Input_address,
  input  We,
  input  Reset,
  input  Clcok,
  output [31:0] Out_data,
  output valid,
  output [27:0] Out_tag,
  output Hit,
  output Miss
);

  wire cache_line_1_out_valid, cache_line_2_out_valid, cache_line_3_out_valid, cache_line_4_out_valid,
       comparator_1_eq;
  wire [27:0] cache_line_1_out_tag, cache_line_2_out_tag, cache_line_3_out_tag, cache_line_4_out_tag,
       undriven;
  wire [31:0] cache_line_1_out_data, cache_line_2_out_data, cache_line_3_out_data, cache_line_4_out_data;

  cache_line cache_line_1 (
    .In_data(Input_data), .Clock(Clcok), .Out_data(cache_line_1_out_data),
    .Out_valid(cache_line_1_out_valid), .We(We), .In_Offset(Input_address[1:0]), .In_tag(undriven),
    .Out_tag(cache_line_1_out_tag), .Reset(Reset));
  cache_line cache_line_2 (
    .In_data(Input_data), .Clock(Clcok), .Out_data(cache_line_2_out_data),
    .Out_valid(cache_line_2_out_valid), .We(We), .In_Offset(Input_address[1:0]), .In_tag(undriven),
    .Out_tag(cache_line_2_out_tag), .Reset(Reset));
  cache_line cache_line_3 (
    .In_data(Input_data), .Clock(Clcok), .Out_data(cache_line_3_out_data),
    .Out_valid(cache_line_3_out_valid), .We(We), .In_Offset(Input_address[1:0]), .In_tag(undriven),
    .Out_tag(cache_line_3_out_tag), .Reset(Reset));
  cache_line cache_line_4 (
    .In_data(Input_data), .Clock(Clcok), .Out_data(cache_line_4_out_data),
    .Out_valid(cache_line_4_out_valid), .We(We), .In_Offset(Input_address[1:0]), .In_tag(undriven),
    .Out_tag(cache_line_4_out_tag), .Reset(Reset));
  Multiplexer #(.select(2), .enable("false")) multiplexer_1 (
    .in0(cache_line_1_out_valid), .in1(cache_line_2_out_valid), .in2(cache_line_3_out_valid),
    .in3(cache_line_4_out_valid), .out(valid), .sel(Input_address[3:2]));
  Multiplexer #(.select(2), .width(32), .enable("false")) multiplexer_2 (
    .in0(cache_line_1_out_data), .in1(cache_line_2_out_data), .in2(cache_line_3_out_data),
    .in3(cache_line_4_out_data), .out(Out_data), .sel(Input_address[3:2]));
  Multiplexer #(.select(2), .width(28), .enable("false")) multiplexer_3 (
    .in0(cache_line_1_out_tag), .in1(cache_line_2_out_tag), .in2(cache_line_3_out_tag),
    .in3(cache_line_4_out_tag), .out(Out_tag), .sel(Input_address[3:2]));
  Comparator #(.width(28), .mode("unsigned")) comparator_1 (
    .a(Out_tag), .b(Input_address[31:4]), .gt(Miss), .eq(comparator_1_eq), .lt(Miss));
  and and_1 (Hit, valid, comparator_1_eq);
endmodule

module Main (
  input  Clock,
  input  Reset
);

  wire cache_1_hit, cache_1_miss, cache_1_valid, testbench_1_we;
  wire [7:0] adder_1_out, adder_2_out, adder_3_out, multiplexer_1_out, register_1_q, register_2_q,
       register_3_q;
  wire [27:0] cache_1_out_tag;
  wire [31:0] cache_1_out_data, testbench_1_out_addr, testbench_1_out_data;

  Testbench testbench_1 (
    .Clock(Clock), .Reset(Reset), .Out_data(testbench_1_out_data), .Out_addr(testbench_1_out_addr),
    .WE(testbench_1_we));
  cache cache_1 (
    .Input_data(testbench_1_out_data), .Input_address(testbench_1_out_addr), .We(testbench_1_we),
    .Reset(Reset), .Clcok(Clock), .Out_data(cache_1_out_data), .valid(cache_1_valid),
    .Out_tag(cache_1_out_tag), .Hit(cache_1_hit), .Miss(cache_1_miss));
  // Probe on testbench_1_out_addr
  Adder adder_1 (.a(8'h1), .b(register_1_q), .out(adder_1_out));  // open: cin, cout
  Adder adder_2 (.a(8'h1), .b(register_2_q), .out(adder_2_out));  // open: cin, cout
  Register register_1 (.D(adder_1_out), .en(cache_1_miss), .Q(register_1_q), .clk(Clock), .clr(Reset));
  Register register_2 (.D(adder_2_out), .en(cache_1_hit), .Q(register_2_q), .clk(Clock), .clr(Reset));
  // Probe on cache_1_out_tag
  Multiplexer #(.width(8), .enable("false")) multiplexer_1 (
    .in0(8'h1), .in1({8{1'b0}}), .out(multiplexer_1_out), .sel(Clock));
  // Probe on cache_1_out_data
  // Probe on cache_1_valid
  Register register_3 (.D(adder_3_out), .Q(register_3_q), .clk(Clock), .clr(Reset));  // open: en
  Adder adder_3 (.a(multiplexer_1_out), .b(register_3_q), .out(adder_3_out));  // open: cin, cout
  // Probe on register_1_q
  // Probe on register_2_q
  // Probe on register_3_q

  // Notes on the sheet:
  //   NOMES DOS AUTORES: José Mikael da Silva Alves - Thiago Henrique Fonseca Pereira
  //   NÃO MODIFICAR NADA NESTE CIRCUITO
  //   Execute a simulação até o total chegar a 27
endmodule

// Cache Tester
module Testbench (
  input  Clock,
  input  Reset,
  output [31:0] Out_data,
  output [31:0] Out_addr,
  output WE
);

  wire [7:0] adder_1_out, counter_1_q, register_1_q;
  wire [31:1] ram_3_data;

  Adder adder_1 (.a(register_1_q), .b(8'h1), .out(adder_1_out));  // open: cin, cout
  Register register_1 (.D(counter_1_q), .Q(register_1_q), .clk(Clock), .clr(Reset));  // open: en
  Counter counter_1 (.D(adder_1_out), .Q(counter_1_q), .clk(Clock), .clr(Reset));  // open: load, count, carry
  RAM #(.dataWidth(32)) ram_1 (.addr(register_1_q), .data(Out_data), .clk(Clock));  // open: sel, ld, clr
  RAM #(.dataWidth(32)) ram_2 (.addr(register_1_q), .data(Out_addr), .clk(Clock));  // open: sel, ld, clr
  RAM #(.dataWidth(32)) ram_3 (.addr(register_1_q), .data({ram_3_data, WE}), .clk(Clock));  // open: sel, ld, clr

  // Notes on the sheet:
  //   Data
  //   Address
  //   We
  //   Inicializar cada memória com os arquivos de mesmo nome e extensão .mem
  //   NÃO MODIFICAR NADA NESTE CIRCUITO
endmodule
